# Fritzing sketch circuit_test (saved by Fritzing 0.9.6b)
breadboards: 1

parts:
  Part5 = I2C level shifter bidirectional
  Mod2 = Raspberry Pi 4B
  Part4 = Arduino Nano (Rev3.0)

nets:
  N1: Part5.LV4, Mod2.GPIO21
  N2: Part5.LV3, Mod2.GPIO20
  GND: Part5.GND, Mod2.GND
  N3: Part5.LV, Mod2.3V3
  N4: Part5.LV2, Mod2.GPIO16
  N5: Part5.HV2, Part4.D3
  N6: Part5.HV, Mod2.5V
  N7: Part5.HV3, Part4.D4
  N8: Part5.HV4, Part4.D2
